// Logisim project SUBTLE_0.circ as structural Verilog: 6 circuits, main circuit main
module main (
);

  wire and_1_out, and_2_out, clock_1_out, controlled_buffer_1_out, ctrl_logic_1_a, ctrl_logic_1_jmp,
       ctrl_logic_1_mar, ctrl_logic_1_pc, ctrl_logic_1_rd, ctrl_logic_1_wr, mapped_io_1_en_in,
       mapped_io_1_en_out, mod5_counter_1_bit_0, mod5_counter_1_bit_1, mod5_counter_1_bit_2,
       neg1_detect_1_r0_notneg1, neg1_detect_1_r1_notneg1, not_1_out, not_2_out, or_1_out, RESET_out,
       subleq_1_leq, undriven;
  wire [6:0] keyboard_1_data, mapped_io_1_output_7;
  wire [15:0] COUNTER_PC_q, multiplexer_1_out, multiplexer_2_out, RAM_128KB_dout, REG_MEMADDR_q,
       subleq_1_reg_bminusa;

  Clock clock_1 (.out(clock_1_out));
  assign controlled_buffer_1_out = neg1_detect_1_r1_notneg1 ? clock_1_out : 1'bz;  // Controlled_Buffer controlled_buffer_1
  NEG1_DETECT neg1_detect_1 (
    .REG_0(multiplexer_1_out), .REG_1(COUNTER_PC_q), .R0_NOTNEG1(neg1_detect_1_r0_notneg1),
    .R1_NOTNEG1(neg1_detect_1_r1_notneg1));
  not not_1 (not_1_out, neg1_detect_1_r0_notneg1);
  Register #(.width(16)) REG_MEMADDR (
    .D(multiplexer_2_out), .en(ctrl_logic_1_mar), .clk(controlled_buffer_1_out), .Q(REG_MEMADDR_q),
    .clr(undriven));
  Counter #(.max('hffff), .width(16)) COUNTER_PC (
    .load(and_1_out), .D(multiplexer_2_out), .count(or_1_out), .Q(COUNTER_PC_q),
    .clk(controlled_buffer_1_out), .clr(RESET_out));  // open: carry, up
  Button RESET (.out(RESET_out));
  MOD5_COUNTER mod5_counter_1 (
    .CLK(controlled_buffer_1_out), .BIT_0(mod5_counter_1_bit_0), .BIT_1(mod5_counter_1_bit_1),
    .BIT_2(mod5_counter_1_bit_2));
  and and_1 (and_1_out, ctrl_logic_1_jmp, subleq_1_leq);
  or or_1 (or_1_out, ctrl_logic_1_rd, and_2_out);
  RAM #(.addrWidth(16), .dataWidth(16), .enables("line")) RAM_128KB (
    .addr(multiplexer_1_out), .we(ctrl_logic_1_wr), .clk(controlled_buffer_1_out),
    .din(subleq_1_reg_bminusa), .dout(RAM_128KB_dout));
  Multiplexer #(.width(16)) multiplexer_1 (
    .in0(COUNTER_PC_q), .in1(REG_MEMADDR_q), .out(multiplexer_1_out), .sel(ctrl_logic_1_rd));
  and and_2 (and_2_out, ctrl_logic_1_jmp, not_2_out);
  not not_2 (not_2_out, subleq_1_leq);
  CTRL_LOGIC ctrl_logic_1 (
    .BIT_0(mod5_counter_1_bit_0), .BIT_1(mod5_counter_1_bit_1), .BIT_2(mod5_counter_1_bit_2),
    .A(ctrl_logic_1_a), .WR(ctrl_logic_1_wr), .RD(ctrl_logic_1_rd), .JMP(ctrl_logic_1_jmp),
    .PC(ctrl_logic_1_pc), .MAR(ctrl_logic_1_mar));
  LED A (.in(ctrl_logic_1_a));
  LED WR (.in(ctrl_logic_1_wr));
  LED RD (.in(ctrl_logic_1_rd));
  LED JMP (.in(ctrl_logic_1_jmp));
  LED PC (.in(ctrl_logic_1_pc));
  LED MAR (.in(ctrl_logic_1_mar));
  TTY tty_1 (.data(mapped_io_1_output_7), .clk(controlled_buffer_1_out), .we(mapped_io_1_en_out), .clr(RESET_out));
  Multiplexer #(.width(16)) multiplexer_2 (
    .in1(RAM_128KB_dout), .out(multiplexer_2_out), .sel(neg1_detect_1_r0_notneg1));  // open: in0
  Keyboard keyboard_1 (
    .clk(controlled_buffer_1_out), .re(mapped_io_1_en_in), .clr(RESET_out), .data(keyboard_1_data));  // open: avail
  MAPPED_IO mapped_io_1 (
    .INPUT_7(keyboard_1_data), .DATA_D_IN(subleq_1_reg_bminusa), .STORE(ctrl_logic_1_wr),
    .sel_INP(ctrl_logic_1_a), .sel_NEG1(not_1_out), .OUTPUT_7(mapped_io_1_output_7),
    .DATA_D_OUT(multiplexer_2_out), .en_OUT(mapped_io_1_en_out), .en_IN(mapped_io_1_en_in));
  SUBLEQ subleq_1 (
    .DATA(multiplexer_2_out), .en_A(ctrl_logic_1_a), .en_LEQ(ctrl_logic_1_wr), .clk(controlled_buffer_1_out),
    .LEQ(subleq_1_leq), .REG_BMINUSA(subleq_1_reg_bminusa));
endmodule

module CTRL_LOGIC (
  input  BIT_0,
  input  BIT_1,
  input  BIT_2,
  output A,
  output WR,
  output RD,
  output JMP,
  output PC,
  output MAR
);

  wire not_1_out, not_2_out, not_3_out;

  not not_1 (not_1_out, BIT_2);
  not not_2 (not_2_out, BIT_1);
  not not_3 (not_3_out, BIT_0);
  and HEX_18 (JMP, BIT_2, not_2_out, not_3_out);
  and HEX_06 (WR, BIT_0, BIT_1, not_1_out);
  and HEX_05 (A, BIT_0, not_2_out, not_1_out);
  and HEX_30 (MAR, not_3_out, not_1_out);
  or or_1 (RD, WR, A);

  assign PC = MAR;
endmodule

module MOD5_COUNTER (
  input  CLK,
  output BIT_0,
  output BIT_1,
  output BIT_2
);

  wire and_1_out, d_ff_1_q, d_ff_2_q, undriven;

  D_Flip_Flop d_ff_1 (.D(BIT_0), .clk(CLK), .Q(d_ff_1_q), .Qn(BIT_0), .preset(and_1_out));  // open: reset
  D_Flip_Flop d_ff_2 (.D(BIT_1), .clk(d_ff_1_q), .Q(d_ff_2_q), .Qn(BIT_1), .preset(and_1_out), .reset(undriven));
  and and_1 (and_1_out, BIT_2, BIT_0);
  D_Flip_Flop d_ff_3 (.D(BIT_2), .clk(d_ff_2_q), .Qn(BIT_2), .preset(and_1_out));  // open: Q, reset
endmodule

module NEG1_DETECT (
  input  [15:0] REG_0,
  input  [15:0] REG_1,
  output R0_NOTNEG1,
  output R1_NOTNEG1
);

  wire comparator_1_gt, comparator_1_lt, comparator_2_gt, comparator_2_lt;

  or or_1 (R0_NOTNEG1, comparator_1_gt, comparator_1_lt);
  Comparator #(.width(16)) comparator_1 (
    .a(REG_0), .b({16{1'b1}}), .gt(comparator_1_gt), .lt(comparator_1_lt));  // open: eq
  or or_2 (R1_NOTNEG1, comparator_2_gt, comparator_2_lt);
  Comparator #(.width(16)) comparator_2 (
    .a(REG_1), .b({16{1'b1}}), .gt(comparator_2_gt), .lt(comparator_2_lt));  // open: eq
endmodule

module SUBLEQ (
  input  [15:0] DATA,
  input  en_A,
  input  en_LEQ,
  input  clk,
  output LEQ,
  output [15:0] REG_BMINUSA
);

  wire comparator_1_eq, comparator_1_gt, or_1_out;
  wire [15:0] REG_A_q;

  Register #(.width(16)) REG_A (.D(DATA), .en(en_A), .clk(clk), .Q(REG_A_q));  // open: clr
  Subtractor #(.width(16)) subtractor_1 (.a(DATA), .b(REG_A_q), .out(REG_BMINUSA));  // open: bin, bout
  or or_1 (or_1_out, comparator_1_gt, comparator_1_eq);
  Comparator #(.width(16)) comparator_1 (
    .a({16{1'b0}}), .b(REG_BMINUSA), .gt(comparator_1_gt), .eq(comparator_1_eq));  // open: lt
  Register #(.width(1)) REG_LEQ (.D(or_1_out), .en(en_LEQ), .clk(clk), .Q(LEQ));  // open: clr
endmodule

module MAPPED_IO (
  input  [6:0] INPUT_7,
  input  [15:0] DATA_D_IN,
  input  STORE,
  input  sel_INP,
  input  sel_NEG1,
  output [6:0] OUTPUT_7,
  output [15:0] DATA_D_OUT,
  output en_OUT,
  output en_IN
);

  wire or_1_out;
  wire [6:0] not_1_out;
  wire [15:0] multiplexer_2_out, negator_1_out;

  assign not_1_out = ~DATA_D_IN[6:0];  // NOT_Gate not_1, 7 bits wide
  Multiplexer #(.width(7)) multiplexer_1 (.in0(INPUT_7), .in1(not_1_out), .out(OUTPUT_7), .sel(STORE));
  Negator #(.width(16)) negator_1 (.in({{9{1'b0}}, INPUT_7}), .out(negator_1_out));
  assign DATA_D_OUT = sel_NEG1 ? multiplexer_2_out : 16'bz;  // Controlled_Buffer controlled_buffer_1
  Multiplexer #(.width(16)) multiplexer_2 (
    .in0({16{1'b1}}), .in1(negator_1_out), .out(multiplexer_2_out), .sel(sel_INP));
  or or_1 (or_1_out, sel_INP, STORE);
  and and_1 (en_OUT, or_1_out, sel_NEG1);
  and and_2 (en_IN, sel_INP, sel_NEG1);
endmodule
