// Logisim project davidar.circ as structural Verilog: 5 circuits, main circuit main
module main (
);

  wire alu_1_leq, and_1_out, clock_1_out, controlled_buffer_1_out, counter_controller_1_cnt,
       counter_controller_1_ld_2, i_o_1_i_en, i_o_1_o_en, n1_1_a_____1, n1_1_b_____1, not_1_out, R_out;
  wire [2:0] MPC_q;
  wire [5:0] rom_1_data;
  wire [6:0] i_o_1_o_data, keyboard_1_data;
  wire [31:0] A_q, alu_1_b_a, counter_controller_1_d_2, MAR_q, multiplexer_1_out, PC_q, ram_1_data;

  assign controlled_buffer_1_out = n1_1_a_____1 ? clock_1_out : 1'bz;  // Controlled_Buffer controlled_buffer_1
  Clock #(.highDuration(1), .lowDuration(1)) clock_1 (.out(clock_1_out));
  Button R (.out(R_out));
  Counter #(.width(3), .max(4), .trigger("rising")) MPC (
    .Q(MPC_q), .clk(controlled_buffer_1_out), .clr(R_out));  // open: load, D, count, carry
  and and_1 (and_1_out, rom_1_data[3], alu_1_leq);
  Counter_controller counter_controller_1 (
    .en(rom_1_data[4]), .ld(and_1_out), .D(ram_1_data), .ld_2(counter_controller_1_ld_2),
    .D_2(counter_controller_1_d_2), .cnt(counter_controller_1_cnt));
  Counter #(.width(32), .max(16777215), .trigger("rising")) PC (
    .load(counter_controller_1_ld_2), .D(counter_controller_1_d_2), .count(counter_controller_1_cnt),
    .Q(PC_q), .clk(controlled_buffer_1_out), .clr(R_out));  // open: carry
  Multiplexer #(.select(1), .width(32)) multiplexer_1 (
    .in0(PC_q), .in1(MAR_q), .out(multiplexer_1_out), .sel(rom_1_data[2]));
  _1 u_1_1 (.A(PC_q), .A_____1(n1_1_a_____1), .B(multiplexer_1_out), .B_____1(n1_1_b_____1));
  Register #(.width(32), .trigger("rising")) MAR (
    .D(ram_1_data), .en(rom_1_data[5]), .Q(MAR_q), .clk(controlled_buffer_1_out), .clr(R_out));
  ROM #(.addrWidth(3), .dataWidth(6)) rom_1 (.addr(MPC_q), .data(rom_1_data));  // open: sel
  Keyboard #(.buflen(32), .trigger("rising")) keyboard_1 (
    .clk(controlled_buffer_1_out), .re(i_o_1_i_en), .clr(R_out), .data(keyboard_1_data));  // open: avail
  RAM #(.addrWidth(24), .dataWidth(32), .bus("separate")) ram_1 (
    .addr(multiplexer_1_out[23:0]), .din(alu_1_b_a), .data(ram_1_data), .str(rom_1_data[1]),
    .sel(n1_1_b_____1), .clk(controlled_buffer_1_out), .clr(R_out));  // open: ld
  not not_1 (not_1_out, n1_1_b_____1);
  I_O i_o_1 (
    .D(alu_1_b_a), .I_en(i_o_1_i_en), .I_data(keyboard_1_data), .O_data(i_o_1_o_data), .O_en(i_o_1_o_en),
    .I_sel(rom_1_data[0]), .str(rom_1_data[1]), .sel(not_1_out), .D_2(ram_1_data));
  ALU alu_1 (
    .B(ram_1_data), .A(A_q), .LEQ(alu_1_leq), .en(rom_1_data[1]), .B_A(alu_1_b_a), .clr(R_out),
    .clk(controlled_buffer_1_out));
  Register #(.width(32), .trigger("rising")) A (
    .D(ram_1_data), .en(rom_1_data[0]), .Q(A_q), .clk(controlled_buffer_1_out), .clr(R_out));
  TTY #(.rows(20), .cols(35), .trigger("rising")) tty_1 (
    .data(i_o_1_o_data), .clk(controlled_buffer_1_out), .we(i_o_1_o_en), .clr(R_out));

  // Notes on the sheet:
  //   Control store
  //   -1
  //   MAR PC JMP RD WR A
  //   contents of rom_1 (hex, n*v repeats v):
  //   30 5 30 6 18
  //   A bus
  //   D bus
  //   B bus
  //   RAM
  //   I/O
  //   Input
  //   ALU
  //   Output
endmodule

module ALU (
  input  en,
  input  [31:0] B,
  input  clr,
  input  clk,
  input  [31:0] A,
  output LEQ,
  output [31:0] B_A
);

  wire comparator_1_eq, comparator_1_gt, or_1_out;

  Comparator #(.width(32), .mode("twosComplement")) comparator_1 (
    .a({32{1'b0}}), .b(B_A), .gt(comparator_1_gt), .eq(comparator_1_eq));  // open: lt
  Subtractor #(.width(32)) subtractor_1 (.a(B), .b(A), .out(B_A));  // open: bin, bout
  D_Flip_Flop #(.trigger("rising")) d_ff_1 (
    .clk(clk), .D(or_1_out), .Q(LEQ), .en(en), .reset(clr));  // open: Qn, preset
  or or_1 (or_1_out, comparator_1_gt, comparator_1_eq);
endmodule

module I_O (
  input  [6:0] I_data,
  input  I_sel,
  input  [31:0] D,
  input  str,
  input  sel,
  output I_en,
  output [6:0] O_data,
  output O_en,
  output [31:0] D_2
);

  wire or_1_out;
  wire [6:0] not_1_out;
  wire [31:0] multiplexer_2_out, negator_1_out;

  and and_1 (I_en, I_sel, sel);
  assign not_1_out = ~D[6:0];  // NOT_Gate not_1, 7 bits wide
  Multiplexer #(.select(1), .width(7)) multiplexer_1 (.in0(I_data), .in1(not_1_out), .out(O_data), .sel(str));
  and and_2 (O_en, or_1_out, sel);
  or or_1 (or_1_out, str, I_sel);
  Negator #(.width(32)) negator_1 (.in({{25{1'b0}}, I_data}), .out(negator_1_out));
  Multiplexer #(.select(1), .width(32)) multiplexer_2 (
    .in0({32{1'b1}}), .in1(negator_1_out), .out(multiplexer_2_out), .sel(I_sel));
  assign D_2 = sel ? multiplexer_2_out : 32'bz;  // Controlled_Buffer controlled_buffer_1
endmodule

module Counter_controller (
  input  en,
  input  ld,
  input  [31:0] D,
  output ld_2,
  output [31:0] D_2,
  output cnt
);

  wire not_1_out;

  and and_1 (ld_2, ld, en);
  not not_1 (not_1_out, ld);
  and and_2 (cnt, not_1_out, en);

  assign D_2 = D;
endmodule

module _1 (
  input  [31:0] A,
  input  [31:0] B,
  output A_____1,
  output B_____1
);

  wire comparator_1_gt, comparator_1_lt, comparator_2_gt, comparator_2_lt;

  Comparator #(.width(32), .mode("twosComplement")) comparator_1 (
    .a(A), .b({32{1'b1}}), .gt(comparator_1_gt), .lt(comparator_1_lt));  // open: eq
  or or_1 (A_____1, comparator_1_lt, comparator_1_gt);
  Comparator #(.width(32), .mode("twosComplement")) comparator_2 (
    .a(B), .b({32{1'b1}}), .gt(comparator_2_gt), .lt(comparator_2_lt));  // open: eq
  or or_2 (B_____1, comparator_2_gt, comparator_2_lt);
endmodule
