// Logisim project logic1.circ as structural Verilog: 1 circuit, main circuit main
// EEPROM MICROCODE
module main (
  output [15:0] out_1
);

  wire and_1_out, and_2_out, and_3_out, clock_1_out, comparator_1_eq, comparator_1_gt, d_ff_1_q, d_ff_2_q,
       LEQ_Reg_q, not_1_out, or_1_out, or_2_out, subtractor_1_bout;
  wire [2:0] d_ff_1_qn;
  wire [5:0] rom_1_data;
  wire [15:0] A_Reg_q, Mem_Addr_Reg_q, multiplexer_1_out, PC_Counter_q, ram_1_data;

  Clock clock_1 (.out(clock_1_out));
  D_Flip_Flop d_ff_1 (
    .clk(clock_1_out), .D(d_ff_1_qn[0]), .Q(d_ff_1_q), .Qn(d_ff_1_qn[0]), .preset(and_2_out));  // open: en, reset
  Register #(.width(16)) Mem_Addr_Reg (
    .D(ram_1_data), .en(rom_1_data[5]), .Q(Mem_Addr_Reg_q), .clk(clock_1_out));  // open: clr
  or or_1 (or_1_out, rom_1_data[2], and_1_out);
  Counter #(.width(16), .max('hffff)) PC_Counter (
    .load(and_3_out), .D(ram_1_data), .count(or_1_out), .Q(PC_Counter_q), .clk(clock_1_out));  // open: carry, clr
  D_Flip_Flop d_ff_2 (
    .clk(d_ff_1_q), .D(d_ff_1_qn[1]), .Q(d_ff_2_q), .Qn(d_ff_1_qn[1]), .preset(and_2_out));  // open: en, reset
  and and_1 (and_1_out, rom_1_data[3], not_1_out);
  not not_1 (not_1_out, LEQ_Reg_q);
  Multiplexer #(.width(16), .enable("false")) multiplexer_1 (
    .in0(PC_Counter_q), .in1(Mem_Addr_Reg_q), .out(multiplexer_1_out), .sel(rom_1_data[2]));
  D_Flip_Flop d_ff_3 (.clk(d_ff_2_q), .D(d_ff_1_qn[2]), .Qn(d_ff_1_qn[2]), .preset(and_2_out));  // open: Q, en, reset
  ROM #(.addrWidth(3), .dataWidth(6)) rom_1 (.addr(d_ff_1_qn), .data(rom_1_data));  // open: sel
  RAM #(.addrWidth(16), .dataWidth(16), .bus("separate")) ram_1 (
    .addr(multiplexer_1_out), .din(out_1), .data(ram_1_data), .str(rom_1_data[1]), .clk(clock_1_out));  // open: sel, ld, clr
  and and_2 (and_2_out, d_ff_1_qn[0], 1'b1, d_ff_1_qn[2]);
  Register #(.width(16)) A_Reg (.D(ram_1_data), .en(rom_1_data[0]), .Q(A_Reg_q), .clk(clock_1_out));  // open: clr
  Subtractor #(.width(16)) subtractor_1 (
    .a(ram_1_data), .b(A_Reg_q), .out(out_1), .bout(subtractor_1_bout));  // open: bin
  Comparator #(.width(16)) comparator_1 (
    .a({16{1'b0}}), .b(out_1), .gt(comparator_1_gt), .eq(comparator_1_eq));  // open: lt
  or or_2 (or_2_out, comparator_1_eq, comparator_1_gt, subtractor_1_bout);
  Register #(.width(1)) LEQ_Reg (.D(or_2_out), .en(rom_1_data[1]), .Q(LEQ_Reg_q), .clk(clock_1_out));  // open: clr
  and and_3 (and_3_out, rom_1_data[3], LEQ_Reg_q);

  // Notes on the sheet:
  //   PC
  //   PC++ if no LEQ
  //   contents of rom_1 (hex, n*v repeats v):
  //   30 5 30 6 18
  //   EEPROM MICROCODE
  //   MODULO 5 COUNTER (Reset to 111)
  //   SUBLEQ 0
  //   PC=M[PC] if LEQ
endmodule
