// Logisim project logic3.circ as structural Verilog: 4 circuits, main circuit main
// EEPROM MICROCODE
module main (
);

  wire and_1_out, and_2_out, clock_1_out, MICROCODE_a, MICROCODE_jmp, MICROCODE_mar, MICROCODE_pc,
       MICROCODE_rd, MICROCODE_wr, MOD5_COUNTER_bit_0, MOD5_COUNTER_bit_1, MOD5_COUNTER_bit_2, not_1_out,
       or_1_out, SUBLEQ_ALU_leq;
  wire [15:0] Mem_Addr_Reg_q, multiplexer_1_out, PC_Counter_q, ram_1_data, SUBLEQ_ALU_res__b_a;

  Clock clock_1 (.out(clock_1_out));
  MODULO_5_COUNTER MOD5_COUNTER (
    .CLK(clock_1_out), .BIT_0(MOD5_COUNTER_bit_0), .BIT_1(MOD5_COUNTER_bit_1), .BIT_2(MOD5_COUNTER_bit_2));
  Register #(.width(16)) Mem_Addr_Reg (
    .D(ram_1_data), .en(MICROCODE_mar), .Q(Mem_Addr_Reg_q), .clk(clock_1_out));  // open: clr
  and and_1 (and_1_out, MICROCODE_jmp, SUBLEQ_ALU_leq);
  or or_1 (or_1_out, MICROCODE_rd, and_2_out);
  Counter #(.width(16), .max('hffff)) PC_Counter (
    .load(and_1_out), .D(ram_1_data), .count(or_1_out), .Q(PC_Counter_q), .clk(clock_1_out));  // open: carry, clr
  and and_2 (and_2_out, MICROCODE_jmp, not_1_out);
  not not_1 (not_1_out, SUBLEQ_ALU_leq);
  Multiplexer #(.width(16), .enable("false")) multiplexer_1 (
    .in0(PC_Counter_q), .in1(Mem_Addr_Reg_q), .out(multiplexer_1_out), .sel(MICROCODE_rd));
  LOGIC_MICROCODE MICROCODE (
    .Counter_Bit_0(MOD5_COUNTER_bit_0), .Counter_Bit_1(MOD5_COUNTER_bit_1),
    .Counter_Bit_2(MOD5_COUNTER_bit_2), .A(MICROCODE_a), .WR(MICROCODE_wr), .RD(MICROCODE_rd),
    .JMP(MICROCODE_jmp), .PC(MICROCODE_pc), .MAR(MICROCODE_mar));
  RAM #(.addrWidth(16), .dataWidth(16), .bus("separate")) ram_1 (
    .addr(multiplexer_1_out), .din(SUBLEQ_ALU_res__b_a), .data(ram_1_data), .str(MICROCODE_wr),
    .clk(clock_1_out));  // open: sel, ld, clr
  LED A (.in(MICROCODE_a));
  LED WR (.in(MICROCODE_wr));
  LED RD (.in(MICROCODE_rd));
  LED JMP (.in(MICROCODE_jmp));
  LED PC (.in(MICROCODE_pc));
  LED MAR (.in(MICROCODE_mar));
  SUBLEQ_ALU SUBLEQ_ALU (
    .DATA__D(ram_1_data), .en__A(MICROCODE_a), .en__LEQ(MICROCODE_wr), .clk(clock_1_out),
    .LEQ(SUBLEQ_ALU_leq), .RES__B_A(SUBLEQ_ALU_res__b_a));

  // Notes on the sheet:
  //   PC=M[PC] if LEQ
  //   PC++ if no LEQ
endmodule

module LOGIC_MICROCODE (
  input  Counter_Bit_0,
  input  Counter_Bit_1,
  input  Counter_Bit_2,
  output A,
  output WR,
  output RD,
  output JMP,
  output PC,
  output MAR
);

  wire not_1_out, not_2_out, not_3_out;

  not not_1 (not_1_out, Counter_Bit_2);
  not not_2 (not_2_out, Counter_Bit_1);
  not not_3 (not_3_out, Counter_Bit_0);
  and _0x18H (JMP, Counter_Bit_2, not_2_out, not_3_out);
  and _0x06H (WR, Counter_Bit_0, Counter_Bit_1, not_1_out);
  and _0x05H (A, Counter_Bit_0, not_2_out, not_1_out);
  and _0x30H (MAR, not_3_out, not_1_out);
  or or_1 (RD, WR, A);

  assign PC = MAR;
endmodule

module MODULO_5_COUNTER (
  input  CLK,
  output BIT_0,
  output BIT_1,
  output BIT_2
);

  wire and_1_out, d_ff_1_q, d_ff_2_q;

  D_Flip_Flop d_ff_1 (.clk(CLK), .D(BIT_0), .Q(d_ff_1_q), .Qn(BIT_0), .preset(and_1_out));  // open: en, reset
  D_Flip_Flop d_ff_2 (.clk(d_ff_1_q), .D(BIT_1), .Q(d_ff_2_q), .Qn(BIT_1), .preset(and_1_out));  // open: en, reset
  D_Flip_Flop d_ff_3 (.clk(d_ff_2_q), .D(BIT_2), .Qn(BIT_2), .preset(and_1_out));  // open: Q, en, reset
  and and_1 (and_1_out, BIT_0, BIT_2);

  // Notes on the sheet:
  //   Mod 5. Reset to 111
endmodule

module SUBLEQ_ALU (
  input  [15:0] DATA__D,
  input  en__A,
  input  en__LEQ,
  input  clk,
  output LEQ,
  output [15:0] RES__B_A
);

  wire comparator_1_eq, comparator_1_gt, or_1_out;
  wire [15:0] A_Reg_q;

  Register #(.width(16)) A_Reg (.D(DATA__D), .en(en__A), .Q(A_Reg_q), .clk(clk));  // open: clr
  Subtractor #(.width(16)) subtractor_1 (.a(DATA__D), .b(A_Reg_q), .out(RES__B_A));  // open: bin, bout
  Comparator #(.width(16)) comparator_1 (
    .a({16{1'b0}}), .b(RES__B_A), .gt(comparator_1_gt), .eq(comparator_1_eq));  // open: lt
  or or_1 (or_1_out, comparator_1_gt, comparator_1_eq);
  Register #(.width(1)) LEQ_Reg (.D(or_1_out), .en(en__LEQ), .Q(LEQ), .clk(clk));  // open: clr
endmodule
