// Logisim project logic4.circ as structural Verilog: 6 circuits, main circuit main
// EEPROM MICROCODE
module main (
);

  wire and_1_out, and_2_out, button_1_out, button_2_out, button_3_out, clock_1_out, controlled_buffer_1_out,
       I_O_in_en, I_O_out_en, MICROCODE_a, MICROCODE_jmp, MICROCODE_mar, MICROCODE_pc, MICROCODE_rd,
       MICROCODE_wr, minus_1_reg0_____1, minus_1_reg1_____1, MOD5_COUNTER_bit_0, MOD5_COUNTER_bit_1,
       MOD5_COUNTER_bit_2, not_1_out, not_2_out, or_1_out, SUBLEQ_ALU_leq;
  wire [6:0] I_O_o_data, keyboard_1_data;
  wire [15:0] Mem_Addr_Reg_q, multiplexer_1_out, PC_Counter_q, ram_1_data, SUBLEQ_ALU_res__b_a;

  Clock clock_1 (.out(clock_1_out));
  assign controlled_buffer_1_out = minus_1_reg1_____1 ? clock_1_out : 1'bz;  // Controlled_Buffer controlled_buffer_1
  MODULO_5_COUNTER MOD5_COUNTER (
    .CLK(controlled_buffer_1_out), .BIT_0(MOD5_COUNTER_bit_0), .BIT_1(MOD5_COUNTER_bit_1),
    .BIT_2(MOD5_COUNTER_bit_2));
  Register #(.width(16)) Mem_Addr_Reg (
    .D(ram_1_data), .en(MICROCODE_mar), .Q(Mem_Addr_Reg_q), .clk(controlled_buffer_1_out));  // open: clr
  and and_1 (and_1_out, MICROCODE_jmp, SUBLEQ_ALU_leq);
  or or_1 (or_1_out, MICROCODE_rd, and_2_out);
  Counter #(.width(16), .max('hffff)) PC_Counter (
    .load(and_1_out), .D(ram_1_data), .count(or_1_out), .Q(PC_Counter_q), .clk(controlled_buffer_1_out),
    .clr(button_1_out));  // open: carry
  Button button_1 (.out(button_1_out));
  and and_2 (and_2_out, MICROCODE_jmp, not_1_out);
  not not_1 (not_1_out, SUBLEQ_ALU_leq);
  Multiplexer #(.width(16), .enable("false")) multiplexer_1 (
    .in0(PC_Counter_q), .in1(Mem_Addr_Reg_q), .out(multiplexer_1_out), .sel(MICROCODE_rd));
  LOGIC_MICROCODE MICROCODE (
    .Counter_Bit_0(MOD5_COUNTER_bit_0), .Counter_Bit_1(MOD5_COUNTER_bit_1),
    .Counter_Bit_2(MOD5_COUNTER_bit_2), .A(MICROCODE_a), .WR(MICROCODE_wr), .RD(MICROCODE_rd),
    .JMP(MICROCODE_jmp), .PC(MICROCODE_pc), .MAR(MICROCODE_mar));
  RAM #(.addrWidth(16), .dataWidth(16), .bus("separate")) ram_1 (
    .addr(multiplexer_1_out), .din(SUBLEQ_ALU_res__b_a), .data(ram_1_data), .str(MICROCODE_wr),
    .sel(minus_1_reg0_____1), .clk(controlled_buffer_1_out));  // open: ld, clr
  LED A (.in(MICROCODE_a));
  LED WR (.in(MICROCODE_wr));
  LED RD (.in(MICROCODE_rd));
  LED JMP (.in(MICROCODE_jmp));
  LED PC (.in(MICROCODE_pc));
  LED MAR (.in(MICROCODE_mar));
  MINUS_ONE_DETECTION minus_1 (
    .REG_0(multiplexer_1_out), .REG_1(PC_Counter_q), .REG0_____1(minus_1_reg0_____1),
    .REG1_____1(minus_1_reg1_____1));
  SUBLEQ_ALU SUBLEQ_ALU (
    .DATA__D(ram_1_data), .en__A(MICROCODE_a), .en__LEQ(MICROCODE_wr), .clk(controlled_buffer_1_out),
    .LEQ(SUBLEQ_ALU_leq), .RES__B_A(SUBLEQ_ALU_res__b_a));
  not not_2 (not_2_out, minus_1_reg0_____1);
  MAPPED_I_O_0xffff I_O (
    .DATA_IN(SUBLEQ_ALU_res__b_a), .I_data(keyboard_1_data), .O_data(I_O_o_data), .STORE(MICROCODE_wr),
    .minus_1_sel(not_2_out), .I_sel(MICROCODE_a), .DATA_OUT(ram_1_data), .OUT_en(I_O_out_en),
    .IN_en(I_O_in_en));
  TTY tty_1 (.data(I_O_o_data), .clk(controlled_buffer_1_out), .we(I_O_out_en), .clr(button_3_out));
  Keyboard keyboard_1 (
    .clk(controlled_buffer_1_out), .re(I_O_in_en), .clr(button_2_out), .data(keyboard_1_data));  // open: avail
  Button button_2 (.out(button_2_out));
  Button button_3 (.out(button_3_out));

  // Notes on the sheet:
  //   PC=M[PC] if LEQ
  //   PC++ if no LEQ
endmodule

module LOGIC_MICROCODE (
  input  Counter_Bit_0,
  input  Counter_Bit_1,
  input  Counter_Bit_2,
  output A,
  output WR,
  output RD,
  output JMP,
  output PC,
  output MAR
);

  wire not_1_out, not_2_out, not_3_out;

  not not_1 (not_1_out, Counter_Bit_1);
  not not_2 (not_2_out, Counter_Bit_2);
  not not_3 (not_3_out, Counter_Bit_0);
  and _0x18H (JMP, Counter_Bit_2, not_1_out, not_3_out);
  and _0x06H (WR, Counter_Bit_0, Counter_Bit_1, not_2_out);
  and _0x05H (A, Counter_Bit_0, not_1_out, not_2_out);
  and _0x30H (MAR, not_3_out, not_2_out);
  or or_1 (RD, WR, A);

  assign PC = MAR;
endmodule

module MODULO_5_COUNTER (
  input  CLK,
  output BIT_0,
  output BIT_1,
  output BIT_2
);

  wire and_1_out, d_ff_1_q, d_ff_2_q;

  D_Flip_Flop d_ff_1 (.clk(CLK), .D(BIT_0), .Q(d_ff_1_q), .Qn(BIT_0), .preset(and_1_out));  // open: en, reset
  D_Flip_Flop d_ff_2 (.clk(d_ff_1_q), .D(BIT_1), .Q(d_ff_2_q), .Qn(BIT_1), .preset(and_1_out));  // open: en, reset
  D_Flip_Flop d_ff_3 (.clk(d_ff_2_q), .D(BIT_2), .Qn(BIT_2), .preset(and_1_out));  // open: Q, en, reset
  and and_1 (and_1_out, BIT_0, BIT_2);

  // Notes on the sheet:
  //   Mod 5. Reset to 111
endmodule

module SUBLEQ_ALU (
  input  [15:0] DATA__D,
  input  en__A,
  input  en__LEQ,
  input  clk,
  output LEQ,
  output [15:0] RES__B_A
);

  wire comparator_1_eq, comparator_1_gt, or_1_out;
  wire [15:0] A_Reg_q;

  Register #(.width(16)) A_Reg (.D(DATA__D), .en(en__A), .Q(A_Reg_q), .clk(clk));  // open: clr
  Subtractor #(.width(16)) subtractor_1 (.a(DATA__D), .b(A_Reg_q), .out(RES__B_A));  // open: bin, bout
  Comparator #(.width(16)) comparator_1 (
    .a({16{1'b0}}), .b(RES__B_A), .gt(comparator_1_gt), .eq(comparator_1_eq));  // open: lt
  or or_1 (or_1_out, comparator_1_gt, comparator_1_eq);
  Register #(.width(1)) LEQ_Reg (.D(or_1_out), .en(en__LEQ), .Q(LEQ), .clk(clk));  // open: clr
endmodule

module MINUS_ONE_DETECTION (
  input  [15:0] REG_0,
  input  [15:0] REG_1,
  output REG0_____1,
  output REG1_____1
);

  wire comparator_1_gt, comparator_1_lt, comparator_2_gt, comparator_2_lt;

  Comparator #(.width(16)) comparator_1 (
    .a(REG_0), .b({16{1'b1}}), .gt(comparator_1_gt), .lt(comparator_1_lt));  // open: eq
  Comparator #(.width(16)) comparator_2 (
    .a(REG_1), .b({16{1'b1}}), .gt(comparator_2_gt), .lt(comparator_2_lt));  // open: eq
  or or_1 (REG0_____1, comparator_1_gt, comparator_1_lt);
  or or_2 (REG1_____1, comparator_2_gt, comparator_2_lt);
endmodule

module MAPPED_I_O_0xffff (
  input  [6:0] I_data,
  input  [15:0] DATA_IN,
  input  STORE,
  input  minus_1_sel,
  input  I_sel,
  output [6:0] O_data,
  output [15:0] DATA_OUT,
  output OUT_en,
  output IN_en
);

  wire or_1_out;
  wire [6:0] not_1_out;
  wire [15:0] multiplexer_2_out, negator_1_out;

  Multiplexer #(.width(7), .enable("false")) multiplexer_1 (.in0(I_data), .in1(not_1_out), .out(O_data), .sel(STORE));
  assign not_1_out = ~DATA_IN[6:0];  // NOT_Gate not_1, 7 bits wide
  Negator #(.width(16)) negator_1 (.in({{9{1'b0}}, I_data}), .out(negator_1_out));
  Multiplexer #(.width(16), .enable("false")) multiplexer_2 (
    .in0({16{1'b1}}), .in1(negator_1_out), .out(multiplexer_2_out), .sel(I_sel));
  assign DATA_OUT = minus_1_sel ? multiplexer_2_out : 16'bz;  // Controlled_Buffer controlled_buffer_1
  or or_1 (or_1_out, STORE, I_sel);
  and O_en (OUT_en, or_1_out, minus_1_sel);
  and I_en (IN_en, minus_1_sel, I_sel);
endmodule
